# Fritzing sketch venkman (saved by Fritzing 0.9.3b)
breadboards: 2

parts:
  D1 = LED_BARGRAPH_10 [package=led_bargaph_10]
  R1 = Resistor [tolerance=±5% resistance=220 package="0805 [SMD]"]
  D2 = LED_BARGRAPH_10 [package=led_bargaph_10]
  R2 = Resistor [tolerance=±5% resistance=220 package="0805 [SMD]"]
  Part1 = Arduino Uno (Rev3)

nets:
  N1: D1.A_A, D1.B_A, D1.C_A, D1.D_A, D1.E_A, D1.F_A, D1.G_A, D1.H_A, D1.I_A, D1.J_A, R1.Pin_0
  N2: R1.Pin_1, R2.Pin_1, Part1.GND
  N3: D2.A_A, D2.B_A, D2.C_A, D2.D_A, D2.E_A, D2.F_A, D2.G_A, D2.H_A, D2.I_A, D2.J_A, R2.Pin_0
